# Fritzing sketch Door Controller 3 (saved by Fritzing 0.9.3b)
breadboards: 2

parts:
  Arduino = Arduino Pro Mini v13
  RC522 = MIFARE RFID-RC522-v2
  LED2 = RGB LED - (4 legs) [package="5 mm [THT]"]
  R3 = Resistor [tolerance=±5% resistance=470k package=THT]
  J2 = Power Jack [package=power_jack_smd]
  IC1 = Voltage Regulator [part_number=L7805CV package=to-220-alt]
  C1 = Ceramic Capacitor [capacitance=100nF package="100 mil [THT, multilayer]"]
  C2 = Ceramic Capacitor [capacitance=100nF package="100 mil [THT, multilayer]"]
  Q2 = Basic FET N-Channel [part_number=IRLB8743PBF package="D2Pak [SMD]"]
  R6 = Resistor [tolerance=±5% resistance=7.5k package=THT]
  Raspberry_Pi1 = Raspberry Pi 2
  L1 = Solenoid
  R7 = Resistor [tolerance=±5% resistance=7.5k package="1206 [SMD]"]
  R8 = Resistor [tolerance=±5% resistance=7.5k package="1206 [SMD]"]
  U1 = RJ45 Jack [package=rj45-8]
  U2 = RJ45 Jack [package=rj45-8]
  R9 = Resistor [tolerance=±5% resistance=220 package=THT]
  LED3 = smd LED [color="Red (633nm)" package="0805 [SMD]"]
  S1 = Square Pushbutton

nets:
  N1: Arduino.VCC, U1.1
  GND: Arduino.GND, RC522.GND, R3.Pin_0, U1.8
  N2: Arduino.A4, U1.3
  N3: Arduino.A5, U1.4
  N4: Arduino.D13/SCK, RC522.SCK
  N5: Arduino.D12/MISO, RC522.MISO
  N6: Arduino.D11_PWM/MOSI, RC522.MOSI
  N7: Arduino.D10_PWM/SS, RC522.SDA
  N8: Arduino.D9_PWM, RC522.RST
  N9: Arduino.D8, U1.6
  N10: Arduino.D7, U1.5
  N11: Arduino.D6_PWM, LED2.green_cathode
  N12: Arduino.D5_PWM, LED2.blue_cathode
  N13: Arduino.D3_PWM, LED2.red_cathode
  N14: RC522.3.3V, U1.2
  N15: LED2.common_anode, R3.Pin_1
  N16: J2.PWR, IC1.IN, C2.0, L1.pin2
  GND_2: J2.GND, IC1.GND, C1.0, C2.1, Q2.source, R6.Pin_0, Raspberry_Pi1.GND, U2.8, R9.Pin_0, S1.leg0
  N17: IC1.OUT, C1.1, Raspberry_Pi1.5V, R7.Pin_1, R8.Pin_1, U2.1
  N18: Q2.Gate, R6.Pin_1, Raspberry_Pi1.GPIO21
  N19: Q2.drain, L1.pin1
  3V3: Raspberry_Pi1.3v3, Raspberry_Pi1.3V3, U2.2
  N20: Raspberry_Pi1.GPIO2, R7.Pin_0, U2.3
  N21: Raspberry_Pi1.GPIO3, R8.Pin_0, U2.4
  N22: Raspberry_Pi1.GPIO5, S1.leg1
  N23: Raspberry_Pi1.GPIO19, U2.6
  N24: Raspberry_Pi1.GPIO20, U2.5
  N25: Raspberry_Pi1.GPIO16, LED3.anode
  N26: R9.Pin_1, LED3.cathode

custom parts:
  MIFARE RFID-RC522-v2: A simple China made RFID-RC522 Reader; do check the pin labels, as this is a MFRC522 based clone.
  Voltage Regulator: Voltage Regulator Standard 7805 5V regulator. IGO (Input Ground Output).
