# Fritzing sketch Door Controller RC522 (saved by Fritzing 0.9.3b)
circuit board: 4.72472cm x 5.37351cm
circuit board: 8.10287cm x 7.8527cm
circuit board: 11.6587cm x 6.78252cm
breadboards: 2

parts:
  Arduino_Uno = Arduino Uno (Rev3)
  LED1 = RGB LED - (4 legs) [package="5 mm [THT]"]
  R2 = Resistor [tolerance=±5% resistance=470k package=THT]
  RC522 = RFID-RC522-v2
  Raspberry_Pi1 = Raspberry Pi 2
  R3 = Resistor [tolerance=±5% resistance=6.8k package="1206 [SMD]"]
  R4 = Resistor [tolerance=±5% resistance=6.8k package="1206 [SMD]"]
  Q1 = Basic FET N-Channel [part_number=IRLB8743PBF package="D2Pak [SMD]"]
  R5 = Resistor [tolerance=±5% resistance=1k package=THT]
  Solenoid = Solenoid
  C1 = Ceramic Capacitor [capacitance=100nF package="100 mil [THT, multilayer]"]
  J1 = Power Jack [package=power_jack_smd]
  C3 = Ceramic Capacitor [capacitance=100nF package="100 mil [THT, multilayer]"]
  C4 = Ceramic Capacitor [capacitance=100nF package="100 mil [THT, multilayer]"]
  C2 = Ceramic Capacitor [capacitance=100nF package="100 mil [THT, multilayer]"]
  U1 = Voltage Regulator - 5V [package="TO220 [THT]"]
  U2 = Voltage Regulator - 5V [package="TO220 [THT]"]

nets:
  N1: Arduino_Uno.A4/SDA, Raspberry_Pi1.GPIO2, R3.Pin_0
  N2: Arduino_Uno.A5/SCL, Raspberry_Pi1.GPIO3, R4.Pin_0
  N3: Arduino_Uno.D9_PWM, RC522.RST
  N4: Arduino_Uno.D10_PWM/SS, RC522.SDA
  N5: Arduino_Uno.D11_PWM/MOSI, RC522.MOSI
  N6: Arduino_Uno.D12/MISO, RC522.MISO
  N7: Arduino_Uno.D13/SCK, RC522.SCK
  GND: Arduino_Uno.GND, R2.Pin_0, RC522.GND, Raspberry_Pi1.GND, Q1.source, R5.Pin_0, C1.1, C3.1, C4.0, C2.0, U1.GND, U2.GND
  N8: Arduino_Uno.D2, Q1.Gate, R5.Pin_1
  N9: Arduino_Uno.D3_PWM, LED1.red_cathode
  N10: Arduino_Uno.D5_PWM, LED1.blue_cathode
  N11: Arduino_Uno.D6_PWM, LED1.green_cathode
  3V3: Arduino_Uno.3V3, RC522.3.3V
  N12: LED1.common_anode, R2.Pin_1
  N13: Raspberry_Pi1.5V, R3.Pin_1, R4.Pin_1, C2.1, U1.output_voltage
  N14: Q1.drain, Solenoid.pin1
  N15: Solenoid.pin2, C1.0, J1.PWR, C3.0, U1.input_voltage, U2.input_voltage
  N16: C4.1, U2.output_voltage

custom parts:
  RFID-RC522-v2: A simple China made RFID-RC522 Reader; do check the pin labels, as this is a MFRC522 based clone.
