# Fritzing sketch Door Controller (saved by Fritzing 0.9.3b)
circuit board: 11.4698cm x 5.56327cm
breadboards: 1

parts:
  Part1 = Arduino Uno (Rev3)
  LED1 = RGB LED - (4 legs) [package="5 mm [THT]"]
  LED2 = LED - 5mm [color="Red (633nm)" package="5 mm [THT]"]
  R1 = Resistor [tolerance=±5% resistance=470k package=THT]
  R2 = Resistor [tolerance=±5% resistance=470k package=THT]
  R3 = Resistor [tolerance=±5% resistance=470k package=THT]
  R4 = Resistor [tolerance=±5% resistance=470k package=THT]
  U1 = ID-12_20 [package=id-12]

nets:
  N1: Part1.D9_PWM, R2.Pin_1
  N2: Part1.D10_PWM/SS, R3.Pin_1
  N3: Part1.D11_PWM/MOSI, R4.Pin_1
  GND: Part1.GND, R1.Pin_0, U1.GNDT, U1.+_-
  N4: Part1.D0/RX, U1.D0
  5V: Part1.5V, LED1.common_anode, U1.5V
  N5: LED1.red_cathode, R2.Pin_0
  N6: LED1.green_cathode, R3.Pin_0
  N7: LED1.blue_cathode, R4.Pin_0
  N8: LED2.cathode, R1.Pin_1
  N9: LED2.anode, U1.LED
